# Fritzing sketch devre (saved by Fritzing 0.9.3b)
breadboards: 1

parts:
  Parça1 = Arduino Uno (Rev3) - ICSP
  ZS-042_RTC1 = ZS-042 RTC Module
  DHT1 = Humidity and Temperature Sensor DHT11
  8x8_LED_Modul_mit_MAX1 = 8x8 LED Modul mit MAX7219 [package=THT]

nets:
  N1: Parça1.A4/SDA, ZS-042_RTC1.SDA
  N2: Parça1.A5/SCL, ZS-042_RTC1.SCL
  N3: Parça1.D10_PWM/SS, 8x8_LED_Modul_mit_MAX1.CS_Eingang
  N4: Parça1.D11_PWM/MOSI, 8x8_LED_Modul_mit_MAX1.DIN_Eingang
  N5: Parça1.D13/SCK, 8x8_LED_Modul_mit_MAX1.CLK_Eingang
  N6: Parça1.D2, DHT1.Data-signal
  VCC: Parça1.5V, ZS-042_RTC1.VCC, DHT1.Vcc, 8x8_LED_Modul_mit_MAX1.VCC_Eingang
  GND: Parça1.GND, ZS-042_RTC1.GND, DHT1.GND_2, 8x8_LED_Modul_mit_MAX1.GND_Eingang

custom parts:
  Humidity and Temperature Sensor DHT11: Digital relative humidity & temperature sensor DHT11
